// Logisim project DLD_Project.circ as structural Verilog: 13 circuits, main circuit main
module main (
  input  in_1,
  input  in_2
);

  wire A_AND_B, A_NAND_B, A_NOR_B, A_OR_B, A_XOR_B, ACC_Read, ACC_Write, ADD, Address_Wriite,
       alu_1_borrow_out, alu_1_carry_out, alu_1_equal, alu_1_greater, alu_1_less, alu_1_zero_flag,
       Carry_Flag, clk_1_clock_out, clock_1_out, CMP, CTN_ENB, CTN_OUT, Data_Write, decoder_1_out7,
       Equal_Flag, Greater_Flag, Halt, Instruction_Read, Instruction_Write, Jump, KB_REG_Read, KD_REG_Load,
       Less_Flag, MAR_Read, MAR_Write, not_1_out, NOT_A, or_1_out, or_2_out, or_3_out, RAM_Read, RAM_Write,
       Read_B, Read_X, Read_Y, Reset_Flags, Reset_out, Stack_Data_Read, Stack_Down, Stack_Up, Stack_Write,
       Step_CTN_Reset, SUB, TTY_Write, Upadate_Display, Upper_Data_Read, Write_B, Write_X, Write_Y, Zero_Flag;
  wire [2:0] step_counter_1_data_out;
  wire [3:0] dipswitch_2_sw3;
  wire [3:3] step_counter_1_data_out_2;
  wire [6:0] keyboard_1_data;
  wire [7:0] frame_buffer_1_out_9, frame_buffer_1_out_10, frame_buffer_1_out_11, frame_buffer_1_out_12,
       frame_buffer_1_out_13, frame_buffer_1_out_14, frame_buffer_1_out_15, frame_buffer_1_out_16;
  wire [14:0] dipswitch_3_sw3;
  wire [14:7] rom_3_data;
  wire [15:0] accumulator_1_always_out, b_resgister_1_always_out, instruction_register_1_always_out,
       memory_address_register_1_always_out, multiplexer_1_out, program_counter_1_always_out, ram_1_dout,
       stack_1_stack_data_out;

  Pull_Resistor pull_resistor_1 (.node(dipswitch_2_sw3[3]));
  DipSwitch #(.number(5)) dipswitch_1 (
    .sw1(dipswitch_3_sw3[14]), .sw2(dipswitch_3_sw3[13]), .sw3(dipswitch_3_sw3[12]),
    .sw4(dipswitch_3_sw3[11]), .sw5(dipswitch_3_sw3[10]));
  or or_1 (or_1_out, decoder_1_out7, Step_CTN_Reset, Reset_out);
  not not_1 (not_1_out, clk_1_clock_out);
  Hex_Digit_Display hex_digit_display_1 (.value(dipswitch_2_sw3));  // open: dp
  DipSwitch #(.number(7)) dipswitch_2 (
    .sw1(dipswitch_2_sw3[2]), .sw2(dipswitch_2_sw3[1]), .sw3(dipswitch_2_sw3[0]), .sw4(dipswitch_3_sw3[6]),
    .sw5(dipswitch_3_sw3[5]), .sw6(dipswitch_3_sw3[4]), .sw7(dipswitch_3_sw3[3]));
  Hex_Digit_Display hex_digit_display_2 (.value(dipswitch_3_sw3[6:3]));  // open: dp
  DipSwitch #(.number(3)) dipswitch_3 (.sw1(dipswitch_3_sw3[2]), .sw2(dipswitch_3_sw3[1]), .sw3(dipswitch_3_sw3[0]));
  LED led_1 (.in(instruction_register_1_always_out[15]));
  LED led_2 (.in(step_counter_1_data_out_2[3]));
  Stack stack_1 (
    .Data_IN(stack_1_stack_data_out), .Stack_Reset(Reset_out), .Stack_Down(Stack_Up), .Stack_Up(Stack_Down),
    .Stack_Write(Stack_Write), .Stack_Read(Stack_Data_Read), .Clock(clk_1_clock_out),
    .Stack_Data_OUT(stack_1_stack_data_out));
  LED led_3 (.in(instruction_register_1_always_out[12]));
  LED led_4 (.in(instruction_register_1_always_out[11]));
  LED led_5 (.in(instruction_register_1_always_out[14]));
  LED led_6 (.in(instruction_register_1_always_out[13]));
  LED led_7 (.in(step_counter_1_data_out[0]));
  LED led_8 (.in(step_counter_1_data_out[2]));
  LED led_9 (.in(step_counter_1_data_out[1]));
  Step_Counter step_counter_1 (
    .Reset(or_1_out), .Clock(not_1_out), .Data_OUT({step_counter_1_data_out_2[3], step_counter_1_data_out}));
  ROM #(.addrWidth(16), .dataWidth(16)) rom_1 (
    .addr(multiplexer_1_out),
    .data({Stack_Data_Read, Upper_Data_Read, ACC_Read, CMP, SUB, ADD, Stack_Up, KB_REG_Read, Read_B, Read_Y, Read_X, Instruction_Read, MAR_Read, CTN_ENB, RAM_Read, CTN_OUT}));
  Multiplexer #(.width(16)) multiplexer_1 (
    .in0({1'b0, Carry_Flag, Greater_Flag, Equal_Flag, Zero_Flag, Less_Flag, instruction_register_1_always_out[14:8], step_counter_1_data_out}),
    .in1({dipswitch_2_sw3[3], dipswitch_3_sw3[14:10], dipswitch_2_sw3[2:0], dipswitch_3_sw3[6:0]}),
    .out(multiplexer_1_out), .sel(in_2));
  ROM #(.addrWidth(16), .dataWidth(16)) rom_2 (
    .addr(multiplexer_1_out),
    .data({Upadate_Display, Data_Write, Jump, Stack_Down, Stack_Write, RAM_Write, KD_REG_Load, TTY_Write, Address_Wriite, Write_Y, Write_X, Reset_Flags, Write_B, ACC_Write, Instruction_Write, MAR_Write}));
  ROM #(.addrWidth(16), .dataWidth(16)) rom_3 (
    .addr(multiplexer_1_out),
    .data({Halt, rom_3_data, Step_CTN_Reset, A_NOR_B, A_NAND_B, A_XOR_B, A_OR_B, A_AND_B, NOT_A}));
  RAM #(.addrWidth(16), .dataWidth(16), .enables("line")) ram_1 (
    .addr(memory_address_register_1_always_out), .we(RAM_Write), .clk(clk_1_clock_out),
    .din(stack_1_stack_data_out), .dout(ram_1_dout));
  Instruction_Register instruction_register_1 (
    .Data_IN(stack_1_stack_data_out), .Write(Instruction_Write), .Read_To_Lower(Instruction_Read),
    .Read_to_Upper(Upper_Data_Read), .Reset(Reset_out), .Clock(clk_1_clock_out),
    .Always_OUT(instruction_register_1_always_out), .Data_OUT_To_Lower(stack_1_stack_data_out[15:8]),
    .Data_OUT_To_Upper(stack_1_stack_data_out[7:0]));
  LED led_10 (.in(instruction_register_1_always_out[10]));
  LED led_11 (.in(instruction_register_1_always_out[9]));
  LED led_12 (.in(instruction_register_1_always_out[8]));
  LED led_13 (.in(instruction_register_1_always_out[7]));
  Decoder #(.select(4)) decoder_1 (
    .out7(decoder_1_out7), .sel({step_counter_1_data_out_2[3], step_counter_1_data_out}));  // open: out0, out1, out2, out3, out4, out5, out6, out8, out9, out10, out11, out12, out13, out14, out15, en
  LED led_14 (.in(instruction_register_1_always_out[6]));
  LED led_15 (.in(instruction_register_1_always_out[5]));
  LED led_16 (.in(instruction_register_1_always_out[4]));
  LED led_17 (.in(instruction_register_1_always_out[3]));
  Clock clock_1 (.out(clock_1_out));
  Memory_Address_Register memory_address_register_1 (
    .Data_IN(stack_1_stack_data_out), .MAR_Write(MAR_Write), .MAR_Read(MAR_Read), .Clock(clk_1_clock_out),
    .Reset(Reset_out), .Always_OUT(memory_address_register_1_always_out), .Data_OUt(stack_1_stack_data_out));
  LED led_18 (.in(instruction_register_1_always_out[2]));
  LED led_19 (.in(instruction_register_1_always_out[1]));
  LED led_20 (.in(instruction_register_1_always_out[0]));
  CLK clk_1 (
    .Clock_Enable(in_1), .Halt(Halt), .Clock_IN(clock_1_out), .Clock_OUT(clk_1_clock_out));  // open: Manual_Tick
  assign stack_1_stack_data_out = RAM_Read ? ram_1_dout : 16'bz;  // Controlled_Buffer controlled_buffer_1
  LED led_21 (.in(stack_1_stack_data_out[15]));
  LED led_22 (.in(stack_1_stack_data_out[14]));
  LED led_23 (.in(stack_1_stack_data_out[13]));
  Pull_Resistor pull_resistor_2 (.node(stack_1_stack_data_out[15]));
  Pull_Resistor pull_resistor_3 (.node(stack_1_stack_data_out[14]));
  Pull_Resistor pull_resistor_4 (.node(stack_1_stack_data_out[13]));
  LED led_24 (.in(stack_1_stack_data_out[12]));
  LED led_25 (.in(stack_1_stack_data_out[11]));
  LED led_26 (.in(stack_1_stack_data_out[10]));
  LED led_27 (.in(stack_1_stack_data_out[9]));
  Pull_Resistor pull_resistor_5 (.node(stack_1_stack_data_out[12]));
  Pull_Resistor pull_resistor_6 (.node(stack_1_stack_data_out[11]));
  Pull_Resistor pull_resistor_7 (.node(stack_1_stack_data_out[10]));
  Pull_Resistor pull_resistor_8 (.node(stack_1_stack_data_out[9]));
  LED led_28 (.in(stack_1_stack_data_out[8]));
  LED led_29 (.in(stack_1_stack_data_out[7]));
  LED led_30 (.in(stack_1_stack_data_out[6]));
  LED led_31 (.in(stack_1_stack_data_out[5]));
  Pull_Resistor pull_resistor_9 (.node(stack_1_stack_data_out[8]));
  Pull_Resistor pull_resistor_10 (.node(stack_1_stack_data_out[7]));
  Pull_Resistor pull_resistor_11 (.node(stack_1_stack_data_out[6]));
  Pull_Resistor pull_resistor_12 (.node(stack_1_stack_data_out[5]));
  LED led_32 (.in(stack_1_stack_data_out[4]));
  LED led_33 (.in(stack_1_stack_data_out[3]));
  LED led_34 (.in(stack_1_stack_data_out[2]));
  LED led_35 (.in(stack_1_stack_data_out[1]));
  Pull_Resistor pull_resistor_13 (.node(stack_1_stack_data_out[4]));
  Pull_Resistor pull_resistor_14 (.node(stack_1_stack_data_out[3]));
  Pull_Resistor pull_resistor_15 (.node(stack_1_stack_data_out[2]));
  Pull_Resistor pull_resistor_16 (.node(stack_1_stack_data_out[1]));
  LED led_36 (.in(stack_1_stack_data_out[0]));
  Pull_Resistor pull_resistor_17 (.node(stack_1_stack_data_out[0]));
  LED led_37 (.in(program_counter_1_always_out[15]));
  LED led_38 (.in(program_counter_1_always_out[14]));
  LED led_39 (.in(program_counter_1_always_out[13]));
  LED led_40 (.in(program_counter_1_always_out[12]));
  LED led_41 (.in(program_counter_1_always_out[11]));
  LED led_42 (.in(program_counter_1_always_out[10]));
  LED led_43 (.in(program_counter_1_always_out[9]));
  LED led_44 (.in(program_counter_1_always_out[8]));
  LED led_45 (.in(program_counter_1_always_out[7]));
  LED led_46 (.in(program_counter_1_always_out[6]));
  LED led_47 (.in(program_counter_1_always_out[5]));
  LED led_48 (.in(program_counter_1_always_out[4]));
  Program_Counter program_counter_1 (
    .Reset(Reset_out), .Jump(Jump), .Counter_Enable(CTN_ENB), .Clock(clk_1_clock_out),
    .Address_IN(stack_1_stack_data_out), .Counter_OUT(CTN_OUT), .Always_OUT(program_counter_1_always_out),
    .Address_OUT(stack_1_stack_data_out));
  B_Resgister b_resgister_1 (
    .B_Write(Write_B), .B_Read(Read_B), .Clock(clk_1_clock_out), .Reset(Reset_out),
    .Always_OUT(b_resgister_1_always_out), .Data_OUT(stack_1_stack_data_out));  // open: Data_IN
  X_AND_Y_Register x_and_y_register_1 (
    .Data_IN(stack_1_stack_data_out), .Write_X(Write_X), .Write_Y(Write_Y), .Read_X(Read_X), .Read_Y(Read_Y),
    .Clock(clk_1_clock_out), .Reset(Reset_out), .Data_OUT(stack_1_stack_data_out));  // open: X_Always_OUT, Y_Always_OUT
  TTY tty_1 (.data(stack_1_stack_data_out[6:0]), .clk(clk_1_clock_out), .we(TTY_Write), .clr(Reset_out));
  LED led_49 (.in(program_counter_1_always_out[3]));
  LED led_50 (.in(program_counter_1_always_out[2]));
  LED led_51 (.in(program_counter_1_always_out[1]));
  LED led_52 (.in(program_counter_1_always_out[0]));
  Accumulator accumulator_1 (
    .A_Write(ACC_Write), .A_Read(ACC_Read), .Clock(clk_1_clock_out), .Reset(Reset_out),
    .Data_IN(stack_1_stack_data_out), .Always_OUT(accumulator_1_always_out), .Data_OUT(stack_1_stack_data_out));
  Keyboard keyboard_1 (.clk(KD_REG_Load), .data(keyboard_1_data));  // open: re, clr, avail
  ALU alu_1 (
    .ADD(ADD), .SUB(SUB), .A_IN(accumulator_1_always_out), .B_IN(b_resgister_1_always_out), .NOT_A(NOT_A),
    .A_AND_B(A_AND_B), .A_OR_B(A_OR_B), .A_NAND_B(A_NAND_B), .A_NOR_B(A_NOR_B), .A_XOR_B(A_XOR_B),
    .Carry_OUT(alu_1_carry_out), .Borrow_OUT(alu_1_borrow_out), .Zero_Flag(alu_1_zero_flag),
    .Greater(alu_1_greater), .Equal(alu_1_equal), .Less(alu_1_less), .Data_OUT(stack_1_stack_data_out));  // open: Borrow_IN, Carry_IN
  or or_2 (or_2_out, SUB, ADD);
  buf or_3 (or_3_out, Reset_Flags);  // OR_Gate
  assign stack_1_stack_data_out[6:0] = KB_REG_Read ? keyboard_1_data : 7'bz;  // Controlled_Buffer controlled_buffer_2
  DotMatrix #(.inputtype("row"), .matrixcols(8), .matrixrows(8)) dotmatrix_1 (
    .row0(frame_buffer_1_out_9), .row1(frame_buffer_1_out_10), .row2(frame_buffer_1_out_11),
    .row3(frame_buffer_1_out_12), .row4(frame_buffer_1_out_13), .row5(frame_buffer_1_out_14),
    .row6(frame_buffer_1_out_15), .row7(frame_buffer_1_out_16));
  Frame_Buffer frame_buffer_1 (
    .Data_Write_Enable(Data_Write), .Address_Selector(stack_1_stack_data_out[2:0]),
    .Buffer_Address_Write_Enable(Address_Wriite), .Clock(clk_1_clock_out), .Reset_Buffer(Reset_out),
    .Update_Display(Upadate_Display), .Reset_Display(Reset_out), .Data_IN(stack_1_stack_data_out[7:0]),
    .out_9(frame_buffer_1_out_9), .out_10(frame_buffer_1_out_10), .out_11(frame_buffer_1_out_11),
    .out_12(frame_buffer_1_out_12), .out_13(frame_buffer_1_out_13), .out_14(frame_buffer_1_out_14),
    .out_15(frame_buffer_1_out_15), .out_16(frame_buffer_1_out_16));
  Flags_Register flags_register_1 (
    .Carry(alu_1_carry_out), .Borrow(alu_1_borrow_out), .Greater(alu_1_greater), .Equals(alu_1_equal),
    .Less(alu_1_less), .Zero(alu_1_zero_flag), .Math_Flag_Set(or_2_out), .Compare_Flag_Set(CMP),
    .Clock(clk_1_clock_out), .Reset(or_3_out), .Carry_Flag(Carry_Flag), .Greater_flag(Greater_Flag),
    .Equal_Flag(Equal_Flag), .Less_Flag(Less_Flag), .Zero_Flag(Zero_Flag));  // open: Borrow_Flag
  Button Reset (.out(Reset_out));

  // Notes on the sheet:
  //   contents of rom_1 (hex, n*v repeats v):
  //   1 6 6*0 1 6 10 2 4*0 1 6 10 2 4*0 1 6 10 2 4*0 1 6 10 2 4*0 1 6 10 2 4*0 1 6 10 5*0 1 6 10 1 4*0 1 6
  //   10 5*0 1 6 10 5*0 1 6 10 5*0 1 6 10 2000 4*0 1 6 10 80 4*0 1 6 10 20 4*0 1 6 10 40 4*0 1 6 10 100
  //   4*0 1 6 10 2 400 0 0 0 1 6 10 2 800 0 0 0 1 6 10 2 1000 0 0 0 1 6 10 400 4*0 1 6 10 800 4*0 1 6 6*0
  //   1 6 6*0 1 6 6*0 1 6 6*0 1 6 6*0 1 6 6*0 1 6 6*0 1 6 6*0 1 6 6*0 1 6 6*0 1 6 6*0 1 6 20 40 4*0 1 6 20
  //   2 4*0 1 6 40 5*0 1 6 6*0 1 6 6*0 1 6 6*0 1 6 6*0 1 6 6*0 1 6 6*0 1 6 6*0 1 6 6*0 1 6 6*0 1 6 6*0 1 6
  //   6*0 1 6 6*0 1 6 6*0 1 6 200 1 10 0 0 0 1 6 8000 5*0 1 6 200 1 4000 400 0 0 1 6 6*0 1 6 6*0 1 6 6*0 1
  //   6 6*0 1 6 6*0 1 6 6*0 1 6 6*0 1 6 6*0 1 6 6*0 1 6 6*0 1 6 6*0 1 6 6*0 1 6 6*0 1 6 10 5*0 1 6 10 5*0
  //   1 6 6*0 1 6 10 2 4*0 1 6 10 2 4*0 1 6 6*0 1 6 6*0 1 6 6*0 1 6 6*0 1 6 6*0 1 6 6*0 1 6 6*0 1 6 6*0 1
  //   6 6*0 1 6 6*0 1 6 6*0 1 6 10 5*0 1 6 10 2 4*0 1 6 10 2 4*0 1 6 10 2 4*0 1 6 6*0 1 6 6*0 1 6 6*0 1 6
  //   6*0 1 6 6*0 1 6 6*0 1 6 6*0 1 6 6*0 1 6 6*0 1 6 6*0 1 6 6*0 1 6 6*0 1 6 6*0 1 6 6*0 1 6 6*0 1 6 6*0
  //   1 6 6*0 1 6 6*0 1 6 6*0 1 6 6*0 1 6 6*0 1 6 6*0 1 6 6*0 1 6 6*0 1 6 6*0 1 6 6*0 1 6 6*0 1 6 6*0 1 6
  //   10 5*0 1 6 6*0 1 6 6*0 1 6 6*0 1 6 6*0 1 6 6*0 1 6 40 5*0 1 6 4000 400 2000 0 0 0 1 6 6*0 1 6 6*0 1
  //   6 6*0 1 6 6*0 1 6 6*0 1 6 6*0 1 6 6*0 1 6 6*0 1 6 6*0 1 6 10 2 4*0 1 6 10 2 4*0 1 6 10 2 4*0 1 6 10
  //   2 4*0 1 6 10 2 4*0 1 6 10 5*0 1 6 10 1 4*0 1 6 10 5*0 1 6 10 5*0 1 6 10 5*0 1 6 10 2000 4*0 1 6 10
  //   80 4*0 1 6 10 20 4*0 1 6 10 40 4*0 1 6 10 100 4*0 1 6 10 2 400 0 0 0 1 6 10 2 800 0 0 0 1 6 10 2
  //   1000 0 0 0 1 6 10 400 4*0 1 6 10 800 4*0 1 6 6*0 1 6 6*0 1 6 6*0 1 6 6*0 1 6 6*0 1 6 6*0 1 6 6*0 1 6
  //   6*0 1 6 6*0 1 6 6*0 1 6 6*0 1 6 20 40 4*0 1 6 20 2 4*0 1 6 40 5*0 1 6 6*0 1 6 6*0 1 6 6*0 1 6 6*0 1
  //   6 6*0 1 6 6*0 1 6 6*0 1 6 6*0 1 6 6*0 1 6 6*0 1 6 6*0 1 6 6*0 1 6 6*0 1 6 200 1 10 0 0 0 1 6 8000
  //   5*0 1 6 200 1 4000 400 0 0 1 6 6*0 1 6 6*0 1 6 6*0 1 6 6*0 1 6 6*0 1 6 6*0 1 6 6*0 1 6 6*0 1 6 6*0 1
  //   6 6*0 1 6 6*0 1 6 6*0 1 6 6*0 1 6 10 5*0 1 6 10 5*0 1 6 6*0 1 6 10 2 4*0 1 6 10 2 4*0 1 6 6*0 1 6
  //   6*0 1 6 6*0 1 6 6*0 1 6 6*0 1 6 6*0 1 6 6*0 1 6 6*0 1 6 6*0 1 6 6*0 1 6 6*0 1 6 10 5*0 1 6 10 2 4*0
  //   1 6 10 2 4*0 1 6 10 2 4*0 1 6 6*0 1 6 6*0 1 6 6*0 1 6 6*0 1 6 6*0 1 6 6*0 1 6 6*0 1 6 6*0 1 6 6*0 1
  //   6 6*0 1 6 6*0 1 6 6*0 1 6 6*0 1 6 6*0 1 6 6*0 1 6 6*0 1 6 6*0 1 6 6*0 1 6 6*0 1 6 6*0 1 6 6*0 1 6
  //   6*0 1 6 6*0 1 6 6*0 1 6 6*0 1 6 6*0 1 6 6*0 1 6 6*0 1 6 10 5*0 1 6 10 5*0 1 6 6*0 1 6 6*0 1 6 6*0 1
  //   6 6*0 1 6 40 5*0 1 6 4000 400 2000 0 0 0 1 6 6*0 1 6 6*0 1 6 6*0 1 6 6*0 1 6 6*0 1 6 6*0 1 6 6*0 1 6
  //   6*0 1 6 6*0 1 6 10 2 4*0 1 6 10 2 4*0 1 6 10 2 4*0 1 6 10 2 4*0 1 6 10 2 4*0 1 6 10 5*0 1 6 10 1 4*0
  //   1 6 10 5*0 1 6 10 5*0 1 6 10 5*0 1 6 10 2000 4*0 1 6 10 80 4*0 1 6 10 20 4*0 1 6 10 40 4*0 1 6 10
  //   100 4*0 1 6 10 2 400 0 0 0 1 6 10 2 800 0 0 0 1 6 10 2 1000 0 0 0 1 6 10 400 4*0 1 6 10 800 4*0 1 6
  //   6*0 1 6 6*0 1 6 6*0 1 6 6*0 1 6 6*0 1 6 6*0 1 6 6*0 1 6 6*0 1 6 6*0 1 6 6*0 1 6 6*0 1 6 20 40 4*0 1
  //   6 20 2 4*0 1 6 40 5*0 1 6 6*0 1 6 6*0 1 6 6*0 1 6 6*0 1 6 6*0 1 6 6*0 1 6 6*0 1 6 6*0 1 6 6*0 1 6
  //   6*0 1 6 6*0 1 6 6*0 1 6 6*0 1 6 200 1 10 0 0 0 1 6 8000 5*0 1 6 200 1 4000 400 0 0 1 6 6*0 1 6 6*0 1
  //   6 6*0 1 6 6*0 1 6 6*0 1 6 6*0 1 6 6*0 1 6 6*0 1 6 6*0 1 6 6*0 1 6 6*0 1 6 6*0 1 6 6*0 1 6 10 5*0 1 6
  //   10 5*0 1 6 6*0 1 6 10 2 4*0 1 6 10 2 4*0 1 6 6*0 1 6 6*0 1 6 6*0 1 6 6*0 1 6 6*0 1 6 6*0 1 6 6*0 1 6
  //   6*0 1 6 6*0 1 6 6*0 1 6 6*0 1 6 10 5*0 1 6 10 2 4*0 1 6 10 2 4*0 1 6 10 2 4*0 1 6 6*0 1 6 6*0 1 6
  //   6*0 1 6 6*0 1 6 6*0 1 6 6*0 1 6 6*0 1 6 6*0 1 6 6*0 1 6 6*0 1 6 6*0 1 6 6*0 1 6 6*0 1 6 6*0 1 6 6*0
  //   1 6 6*0 1 6 6*0 1 6 6*0 1 6 6*0 1 6 6*0 1 6 6*0 1 6 6*0 1 6 6*0 1 6 6*0 1 6 6*0 1 6 6*0 1 6 6*0 1 6
  //   6*0 1 6 10 5*0 1 6 6*0 1 6 10 5*0 1 6 6*0 1 6 6*0 1 6 6*0 1 6 40 5*0 1 6 4000 400 2000 0 0 0 1 6 6*0
  //   1 6 6*0 1 6 6*0 1 6 6*0 1 6 6*0 1 6 6*0 1 6 6*0 1 6 6*0 1 6 6*0 1 6 10 2 4*0 1 6 10 2 4*0 1 6 10 2
  //   4*0 1 6 10 2 4*0 1 6 10 2 4*0 1 6 10 5*0 1 6 10 1 4*0 1 6 10 5*0 1 6 10 5*0 1 6 10 5*0 1 6 10 2000
  //   4*0 1 6 10 80 4*0 1 6 10 20 4*0 1 6 10 40 4*0 1 6 10 200 4*0 1 6 10 2 400 0 0 0 1 6 10 2 800 0 0 0 1
  //   6 10 2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
  //   contents of rom_2 (hex, n*v repeats v):
  //   1 2 6*0 1 2 1 4 4*0 1 2 1 8 4*0 1 2 1 20 4*0 1 2 1 40 4*0 1 2 1 100 4*0 1 2 4 5*0 1 2 8 5*0 1 2 20
  //   5*0 1 2 40 5*0 1 2 100 5*0 1 2 1 400 4*0 1 2 1 400 4*0 1 2 1 400 4*0 1 2 1 400 4*0 1 2 1 400 200 0 0
  //   0 1 2 1 8 4 0 0 0 1 2 1 8 4 0 0 0 1 2 1 8 4*0 1 2 8 4 4*0 1 2 8 4 4*0 1 2 6*0 1 2 6*0 1 2 6*0 1 2
  //   6*0 1 2 6*0 1 2 6*0 1 2 6*0 1 2 6*0 1 2 6*0 1 2 6*0 1 2 6*0 1 2 1 400 4*0 1 2 1 40 4*0 1 2 100 5*0 1
  //   2 6*0 1 2 6*0 1 2 6*0 1 2 6*0 1 2 6*0 1 2 6*0 1 2 6*0 1 2 6*0 1 2 6*0 1 2 6*0 1 2 6*0 1 2 6*0 1 2
  //   6*0 1 2 0 800 2000 0 0 0 1 2 2000 800 1000 0 0 0 1 2 0 800 8 2000 0 0 1 2 6*0 1 2 6*0 1 2 6*0 1 2
  //   6*0 1 2 6*0 1 2 6*0 1 2 6*0 1 2 6*0 1 2 6*0 1 2 6*0 1 2 6*0 1 2 6*0 1 2 6*0 1 2 80 5*0 1 2 4000 5*0
  //   1 2 8000 5*0 1 2 1 80 4*0 1 2 1 4000 4*0 1 2 6*0 1 2 6*0 1 2 6*0 1 2 6*0 1 2 6*0 1 2 6*0 1 2 6*0 1 2
  //   6*0 1 2 6*0 1 2 6*0 1 2 6*0 1 2 1 400 4*0 1 2 1 8 4 0 0 0 1 2 1 8 4 0 0 0 1 2 1 8 4 0 0 0 1 2 6*0 1
  //   2 6*0 1 2 6*0 1 2 6*0 1 2 6*0 1 2 6*0 1 2 6*0 1 2 6*0 1 2 6*0 1 2 6*0 1 2 6*0 1 2 6*0 1 2 6*0 1 2
  //   6*0 1 2 6*0 1 2 6*0 1 2 6*0 1 2 6*0 1 2 6*0 1 2 6*0 1 2 6*0 1 2 6*0 1 2 6*0 1 2 6*0 1 2 6*0 1 2 6*0
  //   1 2 6*0 1 2 6*0 1 2 2000 5*0 1 2 6*0 1 2 6*0 1 2 6*0 1 2 6*0 1 2 6*0 1 2 2000 5*0 1 2 8 4 2000 0 0 0
  //   1 2 6*0 1 2 6*0 1 2 6*0 1 2 6*0 1 2 6*0 1 2 6*0 1 2 6*0 1 2 6*0 1 2 6*0 1 2 1 4 4*0 1 2 1 8 4*0 1 2
  //   1 20 4*0 1 2 1 40 4*0 1 2 1 100 4*0 1 2 4 5*0 1 2 8 5*0 1 2 20 5*0 1 2 40 5*0 1 2 100 5*0 1 2 1 400
  //   4*0 1 2 1 400 4*0 1 2 1 400 4*0 1 2 1 400 4*0 1 2 1 400 200 0 0 0 1 2 1 8 4 0 0 0 1 2 1 8 4 0 0 0 1
  //   2 1 8 4*0 1 2 8 4 4*0 1 2 8 4 4*0 1 2 6*0 1 2 6*0 1 2 6*0 1 2 6*0 1 2 6*0 1 2 6*0 1 2 6*0 1 2 6*0 1
  //   2 6*0 1 2 6*0 1 2 6*0 1 2 1 400 4*0 1 2 1 40 4*0 1 2 100 5*0 1 2 6*0 1 2 6*0 1 2 6*0 1 2 6*0 1 2 6*0
  //   1 2 6*0 1 2 6*0 1 2 6*0 1 2 6*0 1 2 6*0 1 2 6*0 1 2 6*0 1 2 6*0 1 2 0 800 2000 0 0 0 1 2 2000 800
  //   1000 0 0 0 1 2 0 800 8 2000 0 0 1 2 6*0 1 2 6*0 1 2 6*0 1 2 6*0 1 2 6*0 1 2 6*0 1 2 6*0 1 2 6*0 1 2
  //   6*0 1 2 6*0 1 2 6*0 1 2 6*0 1 2 6*0 1 2 80 5*0 1 2 4000 5*0 1 2 8000 5*0 1 2 1 80 4*0 1 2 1 4000 4*0
  //   1 2 6*0 1 2 6*0 1 2 6*0 1 2 6*0 1 2 6*0 1 2 6*0 1 2 6*0 1 2 6*0 1 2 6*0 1 2 6*0 1 2 6*0 1 2 1 400
  //   4*0 1 2 1 8 4 0 0 0 1 2 1 8 4 0 0 0 1 2 1 8 4 0 0 0 1 2 6*0 1 2 6*0 1 2 6*0 1 2 6*0 1 2 6*0 1 2 6*0
  //   1 2 6*0 1 2 6*0 1 2 6*0 1 2 6*0 1 2 6*0 1 2 6*0 1 2 6*0 1 2 6*0 1 2 6*0 1 2 6*0 1 2 6*0 1 2 6*0 1 2
  //   6*0 1 2 6*0 1 2 6*0 1 2 6*0 1 2 6*0 1 2 6*0 1 2 6*0 1 2 6*0 1 2 6*0 1 2 6*0 1 2 2000 5*0 1 2 2000 10
  //   4*0 1 2 6*0 1 2 6*0 1 2 6*0 1 2 6*0 1 2 2000 5*0 1 2 8 4 2000 0 0 0 1 2 6*0 1 2 6*0 1 2 6*0 1 2 6*0
  //   1 2 6*0 1 2 6*0 1 2 6*0 1 2 6*0 1 2 6*0 1 2 1 4 4*0 1 2 1 8 4*0 1 2 1 20 4*0 1 2 1 40 4*0 1 2 1 100
  //   4*0 1 2 4 5*0 1 2 8 5*0 1 2 20 5*0 1 2 40 5*0 1 2 100 5*0 1 2 1 400 4*0 1 2 1 400 4*0 1 2 1 400 4*0
  //   1 2 1 400 4*0 1 2 1 400 200 0 0 0 1 2 1 8 4 0 0 0 1 2 1 8 4 0 0 0 1 2 1 8 4*0 1 2 8 4 4*0 1 2 8 4
  //   4*0 1 2 6*0 1 2 6*0 1 2 6*0 1 2 6*0 1 2 6*0 1 2 6*0 1 2 6*0 1 2 6*0 1 2 6*0 1 2 6*0 1 2 6*0 1 2 1
  //   400 4*0 1 2 1 40 4*0 1 2 100 5*0 1 2 6*0 1 2 6*0 1 2 6*0 1 2 6*0 1 2 6*0 1 2 6*0 1 2 6*0 1 2 6*0 1 2
  //   6*0 1 2 6*0 1 2 6*0 1 2 6*0 1 2 6*0 1 2 0 800 2000 0 0 0 1 2 2000 800 1000 0 0 0 1 2 0 800 8 2000 0
  //   0 1 2 6*0 1 2 6*0 1 2 6*0 1 2 6*0 1 2 6*0 1 2 6*0 1 2 6*0 1 2 6*0 1 2 6*0 1 2 6*0 1 2 6*0 1 2 6*0 1
  //   2 6*0 1 2 80 5*0 1 2 4000 5*0 1 2 8000 5*0 1 2 1 80 4*0 1 2 1 4000 4*0 1 2 6*0 1 2 6*0 1 2 6*0 1 2
  //   6*0 1 2 6*0 1 2 6*0 1 2 6*0 1 2 6*0 1 2 6*0 1 2 6*0 1 2 6*0 1 2 1 400 4*0 1 2 1 8 4 0 0 0 1 2 1 8 4
  //   0 0 0 1 2 1 8 4 0 0 0 1 2 6*0 1 2 6*0 1 2 6*0 1 2 6*0 1 2 6*0 1 2 6*0 1 2 6*0 1 2 6*0 1 2 6*0 1 2
  //   6*0 1 2 6*0 1 2 6*0 1 2 6*0 1 2 6*0 1 2 6*0 1 2 6*0 1 2 6*0 1 2 6*0 1 2 6*0 1 2 6*0 1 2 6*0 1 2 6*0
  //   1 2 6*0 1 2 6*0 1 2 6*0 1 2 6*0 1 2 6*0 1 2 6*0 1 2 2000 5*0 1 2 6*0 1 2 2000 10 4*0 1 2 6*0 1 2 6*0
  //   1 2 6*0 1 2 2000 5*0 1 2 8 4 2000 0 0 0 1 2 6*0 1 2 6*0 1 2 6*0 1 2 6*0 1 2 6*0 1 2 6*0 1 2 6*0 1 2
  //   6*0 1 2 6*0 1 2 1 4 4*0 1 2 1 8 4*0 1 2 1 20 4*0 1 2 1 40 4*0 1 2 1 100 4*0 1 2 4 5*0 1 2 8 5*0 1 2
  //   20 5*0 1 2 40 5*0 1 2 100 5*0 1 2 1 400 4*0 1 2 1 400 4*0 1 2 1 400 4*0 1 2 1 400 4*0 1 2 1 400 200
  //   0 0 0 1 2 1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
  //   contents of rom_3 (hex, n*v repeats v):
  //   643*0 1 8*0 2 7*0 4 7*0 8 998*0 1 8*0 2 7*0 4 7*0 8 998*0 1 8*0 2 7*0 4 7*0 8 998*0 1 8*0 2 7*0 4
  //   7*0 8 998*0 1 8*0 2 7*0 4 7*0 8 998*0 1 8*0 2 7*0 4 7*0 8 998*0 1 8*0 2 7*0 4 7*0 8 998*0 1 8*0 2
  //   7*0 4 7*0 8 998*0 1 8*0 2 7*0 4 7*0 8 998*0 1 8*0 2 7*0 4 7*0 8 1007*0 2 7*0 4 7*0 8 1007*0 2 7*0 4
  //   7*0 8 998*0 1 8*0 2 7*0 4 7*0 8 998*0 1 8*0 2 7*0 4 7*0 8 998*0 1 8*0 2 7*0 4 7*0 8 998*0 1 8*0 2
  //   7*0 4 7*0 8 998*0 1 8*0 2 7*0 4 7*0 8 998*0 1 8*0 2 7*0 4 7*0 8 998*0 1 8*0 2 7*0 4 7*0 8 998*0 1
  //   8*0 2 7*0 4 7*0 8 998*0 1 8*0 2 7*0 4 7*0 8 998*0 1 8*0 2 7*0 4 7*0 8 998*0 1 8*0 2 7*0 4 7*0 8
  //   998*0 1 1 7*0 2 7*0 4 0 0 0 4 0 0 0 8 998*0 1 8*0 2 7*0 4 7*0 8 998*0 1 8*0 2 7*0 4 7*0 8 998*0 1
  //   8*0 2 7*0 4 7*0 8 998*0 1 8*0 2 7*0 4 7*0 8 998*0 1 8*0 2 7*0 4 7*0 8 998*0 1 8*0 2 7*0 4 7*0 8
  //   998*0 1 8*0 2 7*0 4 7*0 8 998*0 1 8*0 2 7*0 4 7*0 8
  //   BUS
endmodule

module CLK (
  input  Clock_IN,
  input  Clock_Enable,
  input  Manual_Tick,
  input  Halt,
  output Clock_OUT
);

  wire and_1_out, and_2_out, not_1_out, not_2_out, or_1_out;

  not not_1 (not_1_out, Clock_Enable);
  and and_1 (and_1_out, Clock_IN, Clock_Enable);
  and and_2 (and_2_out, not_1_out, Manual_Tick);
  or or_1 (or_1_out, and_1_out, and_2_out);
  not not_2 (not_2_out, Halt);
  and and_3 (Clock_OUT, or_1_out, not_2_out);
endmodule

module Program_Counter (
  input  Reset,
  input  Jump,
  input  Counter_Enable,
  input  Clock,
  input  [15:0] Address_IN,
  input  Counter_OUT,
  output [15:0] Always_OUT,
  output [15:0] Address_OUT
);

  Counter #(.max('hffff), .width(16)) counter_1 (
    .clr(Reset), .load(Jump), .up(Counter_Enable), .count(Counter_Enable), .clk(Clock), .D(Address_IN),
    .Q(Always_OUT));  // open: carry
  assign Address_OUT = Counter_OUT ? Always_OUT : 16'bz;  // Controlled_Buffer controlled_buffer_1
endmodule

module Accumulator (
  input  [15:0] Data_IN,
  input  A_Write,
  input  A_Read,
  input  Clock,
  input  Reset,
  output [15:0] Always_OUT,
  output [15:0] Data_OUT
);

  Register #(.width(16)) register_1 (.D(Data_IN), .en(A_Write), .clk(Clock), .Q(Always_OUT), .clr(Reset));
  assign Data_OUT = A_Read ? Always_OUT : 16'bz;  // Controlled_Buffer controlled_buffer_1
endmodule

module ALU (
  input  Borrow_IN,
  input  Carry_IN,
  input  [15:0] A_IN,
  input  [15:0] B_IN,
  input  ADD,
  input  SUB,
  input  NOT_A,
  input  A_AND_B,
  input  A_OR_B,
  input  A_XOR_B,
  input  A_NAND_B,
  input  A_NOR_B,
  output Carry_OUT,
  output Borrow_OUT,
  output Greater,
  output Equal,
  output Less,
  output [15:0] Data_OUT,
  output Zero_Flag
);

  wire and_2_out, and_3_out, and_4_out, and_5_out, and_6_out, and_7_out, and_8_out, and_9_out, and_10_out,
       and_11_out, and_12_out, and_13_out, and_14_out, and_15_out, not_2_out, not_3_out, not_4_out,
       not_5_out, not_6_out, not_7_out, not_8_out, not_9_out, not_10_out, not_11_out, not_12_out, not_13_out,
       not_14_out, not_15_out, not_16_out, not_17_out;
  wire [15:0] adder_1_out, and_1_out, nand_1_out, nor_1_out, not_1_out, or_1_out, or_2_out, subtractor_1_out,
       xor_1_out;

  assign Data_OUT = ADD ? adder_1_out : 16'bz;  // Controlled_Buffer controlled_buffer_1
  Adder #(.width(16)) adder_1 (.a(A_IN), .b(B_IN), .out(adder_1_out), .cin(Carry_IN), .cout(Carry_OUT));
  assign Data_OUT = SUB ? subtractor_1_out : 16'bz;  // Controlled_Buffer controlled_buffer_2
  Subtractor #(.width(16)) subtractor_1 (
    .a(A_IN), .b(B_IN), .out(subtractor_1_out), .bin(Borrow_IN), .bout(Borrow_OUT));
  Comparator #(.width(16)) comparator_1 (.a(A_IN), .b(B_IN), .gt(Greater), .eq(Equal), .lt(Less));
  assign not_1_out = ~A_IN;  // NOT_Gate not_1, 16 bits wide
  assign Data_OUT = NOT_A ? not_1_out : 16'bz;  // Controlled_Buffer controlled_buffer_3
  assign and_1_out = A_IN & B_IN;  // AND_Gate and_1, 16 bits wide
  assign Data_OUT = A_AND_B ? and_1_out : 16'bz;  // Controlled_Buffer controlled_buffer_4
  assign or_1_out = A_IN | B_IN;  // OR_Gate or_1, 16 bits wide
  assign Data_OUT = A_OR_B ? or_1_out : 16'bz;  // Controlled_Buffer controlled_buffer_5
  assign xor_1_out = A_IN ^ B_IN;  // XOR_Gate xor_1, 16 bits wide
  assign Data_OUT = A_XOR_B ? xor_1_out : 16'bz;  // Controlled_Buffer controlled_buffer_6
  assign nand_1_out = ~(A_IN & B_IN);  // NAND_Gate nand_1, 16 bits wide
  assign nor_1_out = ~(A_IN | B_IN);  // NOR_Gate nor_1, 16 bits wide
  assign Data_OUT = A_NAND_B ? nand_1_out : 16'bz;  // Controlled_Buffer controlled_buffer_7
  assign Data_OUT = A_NOR_B ? nor_1_out : 16'bz;  // Controlled_Buffer controlled_buffer_8
  assign or_2_out = Data_OUT;  // OR_Gate or_2, 16 bits wide OR_Gate
  not not_2 (not_2_out, or_2_out[2]);
  not not_3 (not_3_out, or_2_out[3]);
  not not_4 (not_4_out, or_2_out[0]);
  not not_5 (not_5_out, or_2_out[1]);
  and and_2 (and_2_out, not_4_out, not_5_out);
  and and_3 (and_3_out, and_2_out, not_2_out);
  and and_4 (and_4_out, and_3_out, not_3_out);
  not not_6 (not_6_out, or_2_out[4]);
  not not_7 (not_7_out, or_2_out[5]);
  not not_8 (not_8_out, or_2_out[6]);
  not not_9 (not_9_out, or_2_out[7]);
  and and_5 (and_5_out, and_4_out, not_6_out);
  and and_6 (and_6_out, and_5_out, not_7_out);
  and and_7 (and_7_out, and_6_out, not_8_out);
  and and_8 (and_8_out, and_7_out, not_9_out);
  not not_10 (not_10_out, or_2_out[8]);
  not not_11 (not_11_out, or_2_out[9]);
  not not_12 (not_12_out, or_2_out[10]);
  not not_13 (not_13_out, or_2_out[11]);
  and and_9 (and_9_out, and_8_out, not_10_out);
  and and_10 (and_10_out, and_9_out, not_11_out);
  and and_11 (and_11_out, and_10_out, not_12_out);
  and and_12 (and_12_out, and_11_out, not_13_out);
  not not_14 (not_14_out, or_2_out[12]);
  not not_15 (not_15_out, or_2_out[13]);
  not not_16 (not_16_out, or_2_out[14]);
  not not_17 (not_17_out, or_2_out[15]);
  and and_13 (and_13_out, and_12_out, not_14_out);
  and and_14 (and_14_out, and_13_out, not_15_out);
  and and_15 (and_15_out, and_14_out, not_16_out);
  and and_16 (Zero_Flag, and_15_out, not_17_out);
  Pull_Resistor pull_resistor_1 (.node(or_2_out[0]));
  Pull_Resistor pull_resistor_2 (.node(or_2_out[1]));
  Pull_Resistor pull_resistor_3 (.node(or_2_out[2]));
  Pull_Resistor pull_resistor_4 (.node(or_2_out[3]));
  Pull_Resistor pull_resistor_5 (.node(or_2_out[4]));
  Pull_Resistor pull_resistor_6 (.node(or_2_out[5]));
  Pull_Resistor pull_resistor_7 (.node(or_2_out[6]));
  Pull_Resistor pull_resistor_8 (.node(or_2_out[7]));
  Pull_Resistor pull_resistor_9 (.node(or_2_out[8]));
  Pull_Resistor pull_resistor_10 (.node(or_2_out[9]));
  Pull_Resistor pull_resistor_11 (.node(or_2_out[10]));
  Pull_Resistor pull_resistor_12 (.node(or_2_out[11]));
  Pull_Resistor pull_resistor_13 (.node(or_2_out[12]));
  Pull_Resistor pull_resistor_14 (.node(or_2_out[13]));
  Pull_Resistor pull_resistor_15 (.node(or_2_out[14]));
  Pull_Resistor pull_resistor_16 (.node(or_2_out[15]));
endmodule

module Flags_Register (
  input  Carry,
  input  Borrow,
  input  Greater,
  input  Equals,
  input  Less,
  input  Zero,
  input  Math_Flag_Set,
  input  Compare_Flag_Set,
  input  Clock,
  input  Reset,
  output Carry_Flag,
  output Borrow_Flag,
  output Greater_flag,
  output Equal_Flag,
  output Less_Flag,
  output Zero_Flag
);

  Register #(.width(1)) register_1 (.D(Carry), .en(Math_Flag_Set), .clk(Clock), .Q(Carry_Flag), .clr(Reset));
  Register #(.width(1)) register_2 (.D(Borrow), .en(Math_Flag_Set), .clk(Clock), .Q(Borrow_Flag), .clr(Reset));
  Register #(.width(1)) register_3 (.D(Greater), .en(Compare_Flag_Set), .clk(Clock), .Q(Greater_flag), .clr(Reset));
  Register #(.width(1)) register_4 (.D(Equals), .en(Compare_Flag_Set), .clk(Clock), .Q(Equal_Flag), .clr(Reset));
  Register #(.width(1)) register_5 (.D(Less), .en(Compare_Flag_Set), .clk(Clock), .Q(Less_Flag), .clr(Reset));
  Register #(.width(1)) register_6 (.D(Zero), .en(Math_Flag_Set), .clk(Clock), .Q(Zero_Flag), .clr(Reset));
endmodule

module B_Resgister (
  input  [15:0] Data_IN,
  input  B_Write,
  input  B_Read,
  input  Clock,
  input  Reset,
  output [15:0] Always_OUT,
  output [15:0] Data_OUT
);

  Register #(.width(16)) register_1 (.D(Data_IN), .en(B_Write), .clk(Clock), .Q(Always_OUT), .clr(Reset));
  assign Data_OUT = B_Read ? Always_OUT : 16'bz;  // Controlled_Buffer controlled_buffer_1
endmodule

module X_AND_Y_Register (
  input  [15:0] Data_IN,
  input  Write_X,
  input  Write_Y,
  input  Read_X,
  input  Read_Y,
  input  Clock,
  input  Reset,
  output [15:0] X_Always_OUT,
  output [15:0] Data_OUT,
  output [15:0] Y_Always_OUT
);

  Register #(.width(16)) register_1 (.D(Data_IN), .en(Write_X), .clk(Clock), .Q(X_Always_OUT), .clr(Reset));
  Register #(.width(16)) register_2 (.D(Data_IN), .en(Write_Y), .clk(Clock), .Q(Y_Always_OUT), .clr(Reset));
  assign Data_OUT = Read_X ? X_Always_OUT : 16'bz;  // Controlled_Buffer controlled_buffer_1
  assign Data_OUT = Read_Y ? Y_Always_OUT : 16'bz;  // Controlled_Buffer controlled_buffer_2

  // Notes on the sheet:
  //   X
  //   Y
endmodule

module Frame_Buffer (
  input  [7:0] Data_IN,
  input  Data_Write_Enable,
  input  [2:0] Address_Selector,
  input  Buffer_Address_Write_Enable,
  input  Clock,
  input  Reset_Buffer,
  input  Update_Display,
  input  Reset_Display,
  output [7:0] out_9,
  output [7:0] out_10,
  output [7:0] out_11,
  output [7:0] out_12,
  output [7:0] out_13,
  output [7:0] out_14,
  output [7:0] out_15,
  output [7:0] out_16
);

  wire demultiplexer_1_out0, demultiplexer_1_out1, demultiplexer_1_out2, demultiplexer_1_out3,
       demultiplexer_1_out4, demultiplexer_1_out5, demultiplexer_1_out6, demultiplexer_1_out7;
  wire [2:0] register_1_q;
  wire [7:0] register_2_q, register_3_q, register_4_q, register_5_q, register_6_q, register_7_q,
       register_8_q, register_9_q;

  Register #(.width(3)) register_1 (
    .D(Address_Selector), .en(Buffer_Address_Write_Enable), .Q(register_1_q), .clr(Clock));  // open: clk
  Demultiplexer #(.select(3)) demultiplexer_1 (
    .out0(demultiplexer_1_out0), .out1(demultiplexer_1_out1), .out2(demultiplexer_1_out2),
    .out3(demultiplexer_1_out3), .out4(demultiplexer_1_out4), .out5(demultiplexer_1_out5),
    .out6(demultiplexer_1_out6), .out7(demultiplexer_1_out7), .in(Data_Write_Enable), .sel(register_1_q));
  Register register_2 (.D(Data_IN), .en(demultiplexer_1_out0), .clk(Clock), .Q(register_2_q), .clr(Reset_Buffer));
  Register register_3 (.D(Data_IN), .en(demultiplexer_1_out1), .clk(Clock), .Q(register_3_q), .clr(Reset_Buffer));
  Register register_4 (.D(Data_IN), .en(demultiplexer_1_out2), .clk(Clock), .Q(register_4_q), .clr(Reset_Buffer));
  Register register_5 (.D(Data_IN), .en(demultiplexer_1_out3), .clk(Clock), .Q(register_5_q), .clr(Reset_Buffer));
  Register register_6 (.D(Data_IN), .en(demultiplexer_1_out4), .clk(Clock), .Q(register_6_q), .clr(Reset_Buffer));
  Register register_7 (.D(Data_IN), .en(demultiplexer_1_out5), .clk(Clock), .Q(register_7_q), .clr(Reset_Buffer));
  Register register_8 (.D(Data_IN), .en(demultiplexer_1_out6), .clk(Clock), .Q(register_8_q), .clr(Reset_Buffer));
  Register register_9 (.D(Data_IN), .en(demultiplexer_1_out7), .clk(Clock), .Q(register_9_q), .clr(Reset_Buffer));
  Register register_10 (.D(register_2_q), .en(Update_Display), .clk(Clock), .Q(out_9), .clr(Reset_Display));
  Register register_11 (.D(register_3_q), .en(Update_Display), .clk(Clock), .Q(out_10), .clr(Reset_Display));
  Register register_12 (.D(register_4_q), .en(Update_Display), .clk(Clock), .Q(out_11), .clr(Reset_Display));
  Register register_13 (.D(register_5_q), .en(Update_Display), .clk(Clock), .Q(out_12), .clr(Reset_Display));
  Register register_14 (.D(register_6_q), .en(Update_Display), .clk(Clock), .Q(out_13), .clr(Reset_Display));
  Register register_15 (.D(register_7_q), .en(Update_Display), .clk(Clock), .Q(out_14), .clr(Reset_Display));
  Register register_16 (.D(register_8_q), .en(Update_Display), .clk(Clock), .Q(out_15), .clr(Reset_Display));
  Register register_17 (.D(register_9_q), .en(Update_Display), .clk(Clock), .Q(out_16), .clr(Reset_Display));
endmodule

module Memory_Address_Register (
  input  [15:0] Data_IN,
  input  MAR_Write,
  input  MAR_Read,
  input  Clock,
  input  Reset,
  output [15:0] Always_OUT,
  output [15:0] Data_OUt
);

  Register #(.width(16)) register_1 (.D(Data_IN), .en(MAR_Write), .clk(Clock), .Q(Always_OUT), .clr(Reset));
  assign Data_OUt = MAR_Read ? Always_OUT : 16'bz;  // Controlled_Buffer controlled_buffer_1
endmodule

module Instruction_Register (
  input  [15:0] Data_IN,
  input  Write,
  input  Read_To_Lower,
  input  Read_to_Upper,
  input  Reset,
  input  Clock,
  output [15:0] Always_OUT,
  output [7:0] Data_OUT_To_Lower,
  output [7:0] Data_OUT_To_Upper
);

  Register #(.width(16)) register_1 (.D(Data_IN), .en(Write), .clk(Clock), .Q(Always_OUT), .clr(Reset));
  assign Data_OUT_To_Lower = Read_to_Upper ? Always_OUT[7:0] : 8'bz;  // Controlled_Buffer controlled_buffer_1
  Controlled_Buffer #(.width(8)) controlled_buffer_2 (.out(Data_OUT_To_Upper), .en(Read_To_Lower));  // open: in
endmodule

module Step_Counter (
  input  Reset,
  input  Clock,
  output [3:0] Data_OUT
);

  Counter #(.max('hf), .width(4)) counter_1 (
    .clr(Reset), .up(1'b1), .clk(Clock), .Q(Data_OUT));  // open: load, count, D, carry
endmodule

module Stack (
  input  Stack_Reset,
  input  Stack_Down,
  input  Stack_Up,
  input  Stack_Write,
  input  Stack_Read,
  input  [15:0] Data_IN,
  input  Clock,
  output [15:0] Stack_Data_OUT
);

  wire not_1_out, or_1_out;
  wire [7:0] counter_1_q;
  wire [15:0] ram_1_dout;

  not not_1 (not_1_out, Stack_Down);
  or or_1 (or_1_out, Stack_Down, Stack_Up);
  Counter counter_1 (
    .clr(Stack_Reset), .up(not_1_out), .count(or_1_out), .clk(or_1_out), .Q(counter_1_q));  // open: load, D, carry
  RAM #(.dataWidth(16), .enables("line")) ram_1 (
    .addr(counter_1_q), .we(Stack_Write), .clk(Clock), .din(Data_IN), .dout(ram_1_dout));
  assign Stack_Data_OUT = Stack_Read ? ram_1_dout : 16'bz;  // Controlled_Buffer controlled_buffer_1
endmodule
